# Fritzing sketch Esquematico (saved by Fritzing 0.9.10b)
breadboards: 1

parts:
  Raspberry_Pi_1 = Raspberry Pi 3 [part_number=RPI-3-V1.2]
  Mod1 = KY-019 5V Relay Module [package="Breakout board"]  # not connected
  S5 = Limit Switch [package="Breakout Board"]
  S6 = Toggle Switch [package=THT]
  S7 = Limit Switch [package="Breakout Board"]
  S8 = Limit Switch [package="Breakout Board"]
  Sensor_Gas = Pushbutton [package="[THT]"]
  Sensor_Incendio = Pushbutton [package="[THT]"]
  R1 = Resistor [tolerance=±5% power=0.25 resistance=10k package=THT]
  R2 = Resistor [tolerance=±5% power=0.25 resistance=10k package=THT]

nets:
  N1: Raspberry_Pi_1.GIPO4, S6.COM
  N2: Raspberry_Pi_1.GND, Raspberry_Pi_1.GIPO21, S5.G, S6.L2, S7.G, S8.G, R1.Pin_1, R2.Pin_1
  N3: Raspberry_Pi_1.GIPO7, Sensor_Incendio.Pin_1, Sensor_Incendio.Pin_2, R2.Pin_0
  N4: Raspberry_Pi_1.GIPO8, Sensor_Gas.Pin_1, Sensor_Gas.Pin_2, R1.Pin_0
  N5: Raspberry_Pi_1.GIPO25, S8.S
  N6: Raspberry_Pi_1.GIPO24, S7.S
  N7: Raspberry_Pi_1.GIPO23, S5.S
  N8: Raspberry_Pi_1.5V, S5.V, S6.L1, S7.V, S8.V, Sensor_Gas.Pin_3, Sensor_Gas.Pin_4, Sensor_Incendio.Pin_3, Sensor_Incendio.Pin_4

notes:
  GPIO 4 ==> Habilitador de la alarma.
  GPIO 23 ==> Sensor ventana sala.
  GPIO 24 ==> Sensor ventana habitación.
  GPIO 25 ==> Sensor puerta principal.
  GPIO 8 ==> Sensor Gas.
  GPIO 7 ==> Sensor Incendio.
  GPIO 20 ==> Salida alarma.

custom parts:
  KY-019 5V Relay Module: KY-019 5V Relay module, used to control AC circuits. (Special thanks to vanepp for fixing the PCB holes and other errors)
  Limit Switch: Generic limit switch commonly found on 3D printers. Typical lever microswitch mounted on a PCB board with a 3 pin JST XH connector.
